// Logisim project calculadora2.circ as structural Verilog
module meio_somador (
  input  a0,
  input  a1,
  output s0,
  output co0
);

  and and_1 (co0, a0, a1);
  xor xor_1 (s0, a0, a1);
endmodule

module somador_completo (
  input  carryin,
  input  a,
  input  b,
  output s,
  output carryout
);

  wire meio_somador_1_co0, meio_somador_1_s0, meio_somador_2_co0;

  meio_somador meio_somador_1 (.a0(a), .a1(b), .co0(meio_somador_1_co0), .s0(meio_somador_1_s0));
  or or_1 (carryout, meio_somador_1_co0, meio_somador_2_co0);
  meio_somador meio_somador_2 (.a0(carryin), .a1(meio_somador_1_s0), .co0(meio_somador_2_co0), .s0(s));
endmodule

module somador_4bits (
  input  in_1,
  input  in_2,
  input  in_3,
  input  in_4,
  input  in_5,
  input  in_6,
  input  in_7,
  input  in_8,
  input  in_9,
  output s0,
  output s1,
  output s2,
  output s3,
  output overflow,
  output carryout
);

  wire somador_completo_1_carryout, somador_completo_2_carryout, somador_completo_3_carryout;

  somador_completo somador_completo_1 (
    .a(in_2), .b(in_6), .carryin(in_1), .carryout(somador_completo_1_carryout), .s(s0));
  somador_completo somador_completo_2 (
    .a(in_3), .b(in_7), .carryin(somador_completo_1_carryout), .carryout(somador_completo_2_carryout), .s(s1));
  somador_completo somador_completo_3 (
    .a(in_4), .b(in_8), .carryin(somador_completo_2_carryout), .carryout(somador_completo_3_carryout), .s(s2));
  somador_completo somador_completo_4 (
    .a(in_5), .b(in_9), .carryin(somador_completo_3_carryout), .carryout(carryout), .s(s3));

  assign overflow = carryout;
endmodule

module decodificador (
  input  e3,
  input  e2,
  input  e1,
  input  e0,
  output a,
  output b,
  output c,
  output d,
  output e,
  output f,
  output g
);

  wire and_1_out, and_2_out, and_3_out, and_4_out, and_5_out, and_6_out, and_7_out, and_8_out, and_9_out,
       and_10_out, and_11_out, and_12_out, and_13_out, and_14_out, and_15_out, and_16_out, and_17_out,
       and_18_out, and_19_out, and_20_out, and_21_out, and_22_out, and_23_out, and_24_out, and_25_out,
       and_26_out, and_27_out, and_28_out, and_29_out, and_30_out, and_31_out, and_32_out, and_33_out,
       and_34_out, and_35_out, and_36_out, and_37_out, and_38_out, and_39_out, and_40_out, and_41_out,
       and_42_out, and_43_out, and_44_out, and_45_out, and_46_out, and_47_out, and_48_out, not_1_out,
       not_2_out, not_3_out, not_4_out, not_5_out, not_6_out, not_7_out, not_8_out, not_9_out, not_10_out,
       not_11_out, not_12_out, not_13_out, not_14_out, not_15_out, not_16_out, not_17_out, not_18_out,
       not_19_out, not_20_out, not_21_out, not_22_out, not_23_out, not_24_out, not_25_out, not_26_out,
       not_27_out, not_28_out, not_29_out, not_30_out, not_31_out, not_32_out, not_33_out, not_34_out,
       not_35_out, not_36_out, not_37_out, not_38_out, not_39_out, not_40_out, not_41_out, not_42_out,
       not_43_out, not_44_out, or_1_out, or_2_out, or_3_out, or_4_out, or_5_out, or_7_out, or_8_out,
       or_9_out, or_10_out, or_11_out, or_12_out, or_13_out, or_14_out, or_15_out, or_16_out, or_17_out,
       or_18_out, or_19_out, or_20_out, or_21_out;

  not not_1 (not_1_out, e2);
  not not_2 (not_2_out, e0);
  not not_3 (not_3_out, e3);
  not not_4 (not_4_out, e3);
  and and_1 (and_1_out, e3, not_5_out);
  not not_5 (not_5_out, e2);
  not not_6 (not_6_out, e1);
  not not_7 (not_7_out, e3);
  and and_2 (and_2_out, not_7_out, not_8_out);
  not not_8 (not_8_out, e1);
  not not_9 (not_9_out, e2);
  and and_3 (and_3_out, not_9_out, not_10_out);
  not not_10 (not_10_out, e1);
  and and_4 (and_4_out, e2, not_11_out);
  not not_11 (not_11_out, e0);
  and and_5 (and_5_out, e3, e1);
  not not_12 (not_12_out, e3);
  and and_6 (and_6_out, not_12_out, not_13_out);
  not not_13 (not_13_out, e2);
  not not_14 (not_14_out, e1);
  not not_15 (not_15_out, e2);
  not not_16 (not_16_out, e0);
  not not_17 (not_17_out, e3);
  and and_7 (and_7_out, not_17_out, not_18_out);
  not not_18 (not_18_out, e2);
  not not_19 (not_19_out, e0);
  not not_20 (not_20_out, e2);
  and and_8 (and_8_out, not_20_out, e1);
  not not_21 (not_21_out, e1);
  not not_22 (not_22_out, e3);
  and and_9 (and_9_out, not_22_out, not_23_out);
  not not_23 (not_23_out, e1);
  not not_24 (not_24_out, e0);
  not not_25 (not_25_out, e3);
  and and_10 (and_10_out, not_25_out, e1);
  not not_26 (not_26_out, e1);
  not not_27 (not_27_out, e3);
  and and_11 (and_11_out, not_27_out, not_28_out);
  not not_28 (not_28_out, e1);
  not not_29 (not_29_out, e0);
  not not_30 (not_30_out, e2);
  not not_31 (not_31_out, e0);
  not not_32 (not_32_out, e3);
  and and_12 (and_12_out, not_32_out, e1);
  and and_13 (and_13_out, e3, not_33_out);
  not not_33 (not_33_out, e1);
  not not_34 (not_34_out, e2);
  and and_14 (and_14_out, not_34_out, e1);
  and and_15 (and_15_out, e1, not_35_out);
  not not_35 (not_35_out, e0);
  not not_36 (not_36_out, e3);
  and and_16 (and_16_out, not_36_out, e2);
  not not_37 (not_37_out, e1);
  not not_38 (not_38_out, e2);
  and and_17 (and_17_out, not_1_out, not_2_out);
  and and_18 (and_18_out, not_3_out, e1);
  and and_19 (and_19_out, not_4_out, e2);
  and and_20 (and_20_out, e2, e1);
  and and_21 (and_21_out, and_1_out, not_6_out);
  not not_39 (not_39_out, e0);
  or or_1 (or_1_out, and_2_out, and_3_out);
  or or_2 (or_2_out, and_4_out, and_5_out);
  and and_22 (and_22_out, and_6_out, not_14_out);
  and and_23 (and_23_out, not_15_out, not_16_out);
  not not_40 (not_40_out, e0);
  and and_24 (and_24_out, and_7_out, not_19_out);
  and and_25 (and_25_out, and_8_out, e0);
  and and_26 (and_26_out, e2, not_21_out);
  and and_27 (and_27_out, e2, e1);
  not not_41 (not_41_out, e0);
  not not_42 (not_42_out, e1);
  and and_28 (and_28_out, and_9_out, not_24_out);
  and and_29 (and_29_out, and_10_out, e0);
  not not_43 (not_43_out, e3);
  not not_44 (not_44_out, e2);
  and and_30 (and_30_out, e3, not_26_out);
  and and_31 (and_31_out, and_11_out, not_29_out);
  and and_32 (and_32_out, not_30_out, not_31_out);
  and and_33 (and_33_out, and_12_out, e0);
  and and_34 (and_34_out, and_13_out, e0);
  or or_3 (or_3_out, and_14_out, and_15_out);
  and and_35 (and_35_out, and_16_out, not_37_out);
  and and_36 (and_36_out, e3, not_38_out);
  and and_37 (and_37_out, e3, e0);
  or or_4 (or_4_out, and_17_out, and_18_out);
  and and_38 (and_38_out, and_19_out, e0);
  or or_5 (or_5_out, and_20_out, and_21_out);
  and and_39 (and_39_out, e3, not_39_out);
  or or_6 (b, or_1_out, or_2_out);
  or or_7 (or_7_out, and_22_out, and_23_out);
  and and_40 (and_40_out, e1, not_40_out);
  and and_41 (and_41_out, e3, e1);
  and and_42 (and_42_out, e3, e2);
  or or_8 (or_8_out, and_24_out, and_25_out);
  and and_43 (and_43_out, and_26_out, e0);
  and and_44 (and_44_out, and_27_out, not_41_out);
  and and_45 (and_45_out, e3, not_42_out);
  or or_9 (or_9_out, and_28_out, and_29_out);
  and and_46 (and_46_out, not_43_out, e2);
  and and_47 (and_47_out, e3, not_44_out);
  and and_48 (and_48_out, and_30_out, e0);
  or or_10 (or_10_out, and_31_out, and_32_out);
  or or_11 (or_11_out, and_33_out, and_34_out);
  or or_12 (or_12_out, or_3_out, and_35_out);
  or or_13 (or_13_out, and_36_out, and_37_out);
  or or_14 (or_14_out, or_4_out, and_38_out);
  or or_15 (or_15_out, or_5_out, and_39_out);
  or or_16 (or_16_out, or_7_out, and_40_out);
  or or_17 (or_17_out, and_41_out, and_42_out);
  or or_18 (or_18_out, or_8_out, and_43_out);
  or or_19 (or_19_out, and_44_out, and_45_out);
  or or_20 (or_20_out, or_9_out, and_46_out);
  or or_21 (or_21_out, and_47_out, and_48_out);
  or or_22 (f, or_10_out, or_11_out);
  or or_23 (g, or_12_out, or_13_out);
  or or_24 (a, or_14_out, or_15_out);
  or or_25 (c, or_16_out, or_17_out);
  or or_26 (d, or_18_out, or_19_out);
  or or_27 (e, or_20_out, or_21_out);
endmodule

module calculadora_4bits (
  input  in_1,
  input  in_2,
  input  in_3,
  input  in_4,
  input  in_5,
  input  in_6,
  input  in_7,
  input  in_8,
  input  in_9,
  output out_10,
  output out_11,
  output out_12,
  output out_13,
  output out_14,
  output out_15
);

  wire decodificador_1_a, decodificador_1_b, decodificador_1_c, decodificador_1_d, decodificador_1_e,
       decodificador_1_f, decodificador_1_g, decodificador_2_a, decodificador_2_b, decodificador_2_c,
       decodificador_2_d, decodificador_2_e, decodificador_2_f, decodificador_2_g, decodificador_3_a,
       decodificador_3_b, decodificador_3_c, decodificador_3_d, decodificador_3_e, decodificador_3_f,
       decodificador_3_g;

  decodificador decodificador_1 (
    .e3(in_5), .e2(in_3), .e1(in_2), .e0(in_1), .a(decodificador_1_a), .b(decodificador_1_b),
    .c(decodificador_1_c), .d(decodificador_1_d), .e(decodificador_1_e), .f(decodificador_1_f),
    .g(decodificador_1_g));
  somador_4bits somador_4bits_1 (
    .in_2(in_1), .in_3(in_2), .in_4(in_3), .in_5(in_5), .in_6(in_6), .in_7(in_7), .in_8(in_8), .in_9(in_9),
    .in_1(in_4), .carryout(out_14), .s0(out_10), .s1(out_11), .s2(out_12), .s3(out_13), .overflow(out_15));
  decodificador decodificador_2 (
    .e3(in_9), .e2(in_8), .e1(in_7), .e0(in_6), .a(decodificador_2_a), .b(decodificador_2_b),
    .c(decodificador_2_c), .d(decodificador_2_d), .e(decodificador_2_e), .f(decodificador_2_f),
    .g(decodificador_2_g));
  _7_Segment_Display u_7_segment_display_1 (
    .g(decodificador_1_g), .f(decodificador_1_b), .a(decodificador_1_a), .b(decodificador_1_f),
    .e(decodificador_1_c), .d(decodificador_1_d), .c(decodificador_1_e));  // open: dp
  _7_Segment_Display u_7_segment_display_2 (
    .g(decodificador_2_g), .f(decodificador_2_b), .a(decodificador_2_a), .b(decodificador_2_f),
    .e(decodificador_2_c), .d(decodificador_2_d), .c(decodificador_2_e));  // open: dp
  decodificador decodificador_3 (
    .e3(out_13), .e2(out_12), .e1(out_11), .e0(out_10), .a(decodificador_3_a), .b(decodificador_3_b),
    .c(decodificador_3_c), .d(decodificador_3_d), .e(decodificador_3_e), .f(decodificador_3_f),
    .g(decodificador_3_g));
  _7_Segment_Display u_7_segment_display_3 (
    .g(decodificador_3_g), .f(decodificador_3_b), .a(decodificador_3_a), .b(decodificador_3_f),
    .e(decodificador_3_c), .d(decodificador_3_d), .c(decodificador_3_e));  // open: dp
endmodule

module mux_1bit (
  input  in_1,
  input  in_2,
  input  in_3,
  output out_4
);

  wire and_1_out, and_2_out, not_1_out;

  not not_1 (not_1_out, in_1);
  and and_1 (and_1_out, in_1, in_3);
  and and_2 (and_2_out, not_1_out, in_2);
  or or_1 (out_4, and_2_out, and_1_out);
endmodule

module mux_4bits (
  input  op0,
  input  op1,
  input  in_3,
  input  in_4,
  input  in_5,
  input  in_6,
  output out_7
);

  wire and_1_out, and_2_out, and_3_out, and_4_out, not_1_out, not_2_out;

  not not_1 (not_1_out, op0);
  not not_2 (not_2_out, op1);
  and and_1 (and_1_out, not_1_out, not_2_out, in_3);
  and and_2 (and_2_out, not_1_out, op1, in_4);
  and and_3 (and_3_out, op0, not_2_out, in_5);
  and and_4 (and_4_out, op0, op1, in_6);
  or or_1 (out_7, and_1_out, and_2_out, and_3_out, and_4_out);
endmodule

module ula_1bit (
  input  binvert,
  input  carryin,
  input  op0,
  input  op1,
  input  a,
  input  b,
  output saida,
  output carryout
);

  wire and_1_out, mux_1bit_1_out_4, not_1_out, not_2_out, or_1_out, somador_completo_1_s;

  not not_1 (not_1_out, b);
  not not_2 (not_2_out, a);
  mux_1bit mux_1bit_1 (.in_2(b), .in_3(not_1_out), .in_1(binvert), .out_4(mux_1bit_1_out_4));
  and and_1 (and_1_out, a, mux_1bit_1_out_4);
  or or_1 (or_1_out, a, mux_1bit_1_out_4);
  somador_completo somador_completo_1 (
    .a(a), .b(mux_1bit_1_out_4), .carryin(carryin), .carryout(carryout), .s(somador_completo_1_s));
  mux_4bits mux_4bits_1 (
    .in_3(and_1_out), .in_4(or_1_out), .in_5(not_2_out), .in_6(somador_completo_1_s), .op0(op0), .op1(op1),
    .out_7(saida));
endmodule

module ula_4bits (
  input  binvert,
  input  op0,
  input  op1,
  input  b3,
  input  b2,
  input  b1,
  input  b0,
  input  a3,
  input  a2,
  input  a1,
  input  a0,
  output out_12,
  output out_13,
  output out_14,
  output out_15,
  output out_16
);

  wire ula_1bit_1_carryout, ula_1bit_2_carryout, ula_1bit_3_carryout;

  ula_1bit ula_1bit_1 (
    .a(a0), .b(b0), .binvert(binvert), .carryin(binvert), .op0(op0), .op1(op1),
    .carryout(ula_1bit_1_carryout), .saida(out_12));
  ula_1bit ula_1bit_2 (
    .a(a1), .b(b1), .binvert(binvert), .carryin(ula_1bit_1_carryout), .op0(op0), .op1(op1),
    .carryout(ula_1bit_2_carryout), .saida(out_13));
  ula_1bit ula_1bit_3 (
    .a(a2), .b(b2), .binvert(binvert), .carryin(ula_1bit_2_carryout), .op0(op0), .op1(op1),
    .carryout(ula_1bit_3_carryout), .saida(out_14));
  ula_1bit ula_1bit_4 (
    .a(a3), .b(b3), .binvert(binvert), .carryin(ula_1bit_3_carryout), .op0(op0), .op1(op1),
    .carryout(out_16), .saida(out_15));
endmodule
